# Fritzing sketch CerebroAna (saved by Fritzing 0.9.3b)

parts:
  U2 = ESP32S-HiLetgo [part_number=ESP32S-HiLetgo]
  Componente2 = RFID-RC522-v2

nets:
  N1: U2.3.3, Componente2.3.3V
  N2: U2.GPIO5, Componente2.SDA
  N3: U2.GPIO18, Componente2.SCK
  N4: U2.GPIO19, Componente2.MISO
  GND: U2.GND, Componente2.GND
  N5: U2.GPIO22, Componente2.RST
  N6: U2.GPIO23, Componente2.MOSI

notes:
  USB-Connection

custom parts:
  ESP32S-HiLetgo: HiLetgo ESP-WROOM-32 ESP32 ESP-32S Development Board 2.4GHz Dual-Mode WiFi + Bluetooth Dual Cores Microcontroller The ESP32 integrated with Antenna switches, RF Balun, power amplifiers, low-noise amplifiers, filters, and management modules, and the entire solution occupies the least area of PCB. 2.4 GHz Wi-Fi plus Bluetooth dual-mode chip, with TSMC Ultra-low power consumption 40nm technology,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
  RFID-RC522-v2: A simple China made RFID-RC522 Reader; do check the pin labels, as this is a MFRC522 based clone.
