# Fritzing sketch ContadorCorrerDistancia (saved by Fritzing 0.9.3b)

parts:
  U1 = ESP32S-HiLetgo [part_number=ESP32S-HiLetgo]
  Componente1 = RFID-RC522-v2
  U3 = LIPO-1000mAh [package=lipo-1000]
  S6 = SPST Switch [package=r_sw_th]

nets:
  N1: U1.3.3, Componente1.3.3V
  GND: U1.GND, Componente1.GND, U3.-
  N2: U1.VIN, S6.O
  N3: U1.GPIO5, Componente1.SDA
  N4: U1.GPIO18, Componente1.SCK
  N5: U1.GPIO19, Componente1.MISO
  N6: U1.GPIO22, Componente1.RST
  N7: U1.GPIO23, Componente1.MOSI
  N8: U3.+, S6.S

custom parts:
  ESP32S-HiLetgo: HiLetgo ESP-WROOM-32 ESP32 ESP-32S Development Board 2.4GHz Dual-Mode WiFi + Bluetooth Dual Cores Microcontroller The ESP32 integrated with Antenna switches, RF Balun, power amplifiers, low-noise amplifiers, filters, and management modules, and the entire solution occupies the least area of PCB. 2.4 GHz Wi-Fi plus Bluetooth dual-mode chip, with TSMC Ultra-low power consumption 40nm technology,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
  RFID-RC522-v2: A simple China made RFID-RC522 Reader; do check the pin labels, as this is a MFRC522 based clone.
