# Fritzing sketch ContadorPechadasAbdominales (saved by Fritzing 0.9.3b)
breadboards: 1

parts:
  Componente1 = Arduino Mega 2560 (Rev3)
  U1 = ESP32S-HiLetgo [part_number=ESP32S-HiLetgo]
  Componente2 = LCD1602-I2C
  LLC1 = Logic Level Converter [package="Breakout board"]
  Componente3 = RFID-RC522-v2
  Componente4 = Adafruit VL530X Time of Flight Distance Sensor [part_number="Adafruit #3317"]
  S1 = Round Pushbutton [part_number=Negro]
  S2 = Round Pushbutton [part_number=Rojo]
  J1 = Basic Force Sensing Resistor (FSR) [package=THT]
  J2 = Basic Force Sensing Resistor (FSR) [package=THT]
  C1 = Capacitor Polarized [package=cpol-radial-100uf-25v]
  R1 = Resistor [tolerance=±5% resistance=100 package="0402 [SMD]"]
  R2 = Resistor [tolerance=±5% resistance=100 package="0402 [SMD]"]
  R3 = Resistor [tolerance=±5% resistance=1.4k package="0402 [SMD]"]
  R4 = Resistor [tolerance=±5% resistance=1.4k package="0402 [SMD]"]
  BAT1 = BC9VPC [package=bc9vpc]
  S5 = SPST Switch [package=r_sw_th]

nets:
  N1: Componente1.A1, J2.pin_1, R2.Pin_0
  N2: Componente1.A2, J1.pin_1, R1.Pin_0
  N3: Componente1.D21/SCL, Componente2.SCL, LLC1.HV2, Componente4.SCL
  N4: Componente1.D20/SDA, Componente2.SDA, LLC1.HV1, Componente4.SDA
  GND: Componente1.GND, U1.GND, Componente2.GND, LLC1.L-GND, LLC1.H-GND, Componente3.GND, Componente4.GND, C1.-, R1.Pin_1, R2.Pin_1, R3.Pin_1, R4.Pin_1, S5.O
  N5: Componente1.D11_PWM, S2.leg1, R3.Pin_0
  N6: Componente1.D10_PWM, S1.leg1, R4.Pin_0
  3V3: Componente1.3V3, Componente3.3.3V
  VCC: Componente1.5V, U1.VIN, Componente2.VCC, LLC1.HV, Componente4.VCC, S1.leg0, S2.leg0, J1.pin_0, J2.pin_0, BAT1.V+
  N7: Componente1.D5_PWM, Componente3.RST
  N8: Componente1.D50, Componente3.MISO
  N9: Componente1.D51, Componente3.MOSI
  N10: Componente1.D52, Componente3.SCK
  N11: Componente1.D53, Componente3.SDA
  N12: U1.3.3, LLC1.LV
  N13: U1.EN, C1.+
  N14: U1.GPIO21, LLC1.LV1
  N15: U1.GPIO22, LLC1.LV2
  N16: BAT1.V-, S5.S

notes:
  Botón rojo
  Botón negro
  <- Regulador 5V aquí

custom parts:
  ESP32S-HiLetgo: HiLetgo ESP-WROOM-32 ESP32 ESP-32S Development Board 2.4GHz Dual-Mode WiFi + Bluetooth Dual Cores Microcontroller The ESP32 integrated with Antenna switches, RF Balun, power amplifiers, low-noise amplifiers, filters, and management modules, and the entire solution occupies the least area of PCB. 2.4 GHz Wi-Fi plus Bluetooth dual-mode chip, with TSMC Ultra-low power consumption 40nm technology,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
  LCD1602-I2C: A standard character display, usually with 2x16 characters. Comes in many colors with LCM1602 IIC attached.
  Logic Level Converter: 5V to/from 3.3V logic level converter
  RFID-RC522-v2: A simple China made RFID-RC522 Reader; do check the pin labels, as this is a MFRC522 based clone.
  Adafruit VL530X Time of Flight Distance Sensor: The VL53L0X is a Time of Flight distance sensor like no other you've used! The sensor contains a very tiny invisible laser source, and a matching sensor. The VL53L0X can detect the "time of flight", or how long the light has taken to bounce back to the sensor. Since it uses a very narrow light source, it is good for determining distance of only the surface directly in front of it. Unlike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
